# Fritzing sketch remote (saved by Fritzing 0.9.3b)
perfboards: 1

parts:
  Arduino_Pro_Mini_3_3v = Arduino Pro Mini (3.3V)
  Transceiver = NRF24L01+ Breakout Board
  Activity_LED = LED - 3mm [color="Blue (525nm)" package="3 mm [THT]"]
  Low_Battery_LED = LED - 3mm [color="Red (660nm)" package="3 mm [THT]"]
  C2 = Electrolytic Capacitor [capacitance=10μF package="0605 [SMD, electrolytic]"]
  Accelerator = Thumb Joystick
  R1 = Resistor [tolerance=±5% resistance=47k package="0603 [SMD]"]
  R2 = Resistor [tolerance=±5% resistance=330 package="0603 [SMD]"]
  R3 = Resistor [tolerance=±5% resistance=10k package="0603 [SMD]"]
  Battery_Charger = TP4056 [chip_label=TP4056 package="DIP (Dual Inline) [THT]"]
  Li-Ion_cell_18650_-_3_7v = 18650 battery holder [package=battery-18650-kit]
  Power_Switch = SPST Switch [package=switch-spdt-smd]
  Online_State = Momentary Switch [package=ksa_sealed_tac_switch]

nets:
  VCC: Arduino_Pro_Mini_3_3v.VCC, Transceiver.VCC, C2.+, Accelerator.VCC
  GND: Arduino_Pro_Mini_3_3v.GND, Transceiver.GND, Activity_LED.cathode, C2.-, Accelerator.GND, R1.Pin_1, R2.Pin_0, Battery_Charger.pin6, Online_State.1
  N1: Arduino_Pro_Mini_3_3v.RAW, R3.Pin_0, Power_Switch.S
  N2: Arduino_Pro_Mini_3_3v.A1, R1.Pin_0, R3.Pin_1
  N3: Arduino_Pro_Mini_3_3v.A0, Accelerator.VERT
  N4: Arduino_Pro_Mini_3_3v.SCK, Transceiver.SCK, Activity_LED.anode
  N5: Arduino_Pro_Mini_3_3v.MISO, Transceiver.MISO
  N6: Arduino_Pro_Mini_3_3v.MOSI, Transceiver.MOSI
  N7: Arduino_Pro_Mini_3_3v.D8, Transceiver.CS
  N8: Arduino_Pro_Mini_3_3v.D7, Transceiver.CE
  N9: Arduino_Pro_Mini_3_3v.D4, Low_Battery_LED.anode
  N10: Arduino_Pro_Mini_3_3v.D3, Online_State.3
  N11: Low_Battery_LED.cathode, R2.Pin_1
  N12: Battery_Charger.pin3, Power_Switch.P
  N13: Battery_Charger.pin4, Li-Ion_cell_18650_-_3_7v.+
  N14: Battery_Charger.pin5, Li-Ion_cell_18650_-_3_7v.-

custom parts:
  TP4056: A DIP stand-in part for whatever IC you want. With 6 pins on a 300mil dual inline package (DIP) footprint.
  18650 battery holder: 18650 Battery Holder
